# Fritzing sketch Finger-Circuit (saved by Fritzing 0.7.12b)
breadboards: 1

parts:
  Power_plug1 = Power plug [part_number="12V Power plug"]
  D1 = Rectifier Diode [part_number=1N4001 package="300 mil [THT]"]
  K1 = Relay [part_number=LEG-6 package=THT]
  R1 = Resistor [tolerance=±5% resistance=1k package=THT]
  Q1 = NPN-Transistor [part_number=2N2222 package="TO92 [THT]"]
  Arduino1 = Arduino
  K2 = Relay [part_number=LEG-6 package=THT]
  D2 = Rectifier Diode [part_number=1N4001 package="300 mil [THT]"]
  R2 = Resistor [tolerance=±5% resistance=1k package=THT]
  Q2 = NPN-Transistor [part_number=2N2222 package="TO92 [THT]"]
  S1 = Pushbutton [part_number=Locker package=THT]
  S2 = Pushbutton [part_number=Locker package=THT]
  CONN1 = USB connector [part_number=Fingerprint package=THT]

nets:
  N1: Power_plug1.GND, S1.leg1, S2.leg1
  N2: Power_plug1.VCC, K1.C1, K1.C2, K2.C1, K2.C2
  N3: D1.cathode, K1.COIL2
  N4: D1.anode, K1.COIL1, Q1.C
  N5: K1.A, S1.leg0
  N6: R1.Pin_0, Q1.B
  N7: R1.Pin_1, Arduino1.D8
  GND: Q1.E, Arduino1.GND, Q2.E, CONN1.GND, CONN1.chassis6
  N8: Arduino1.D9, R2.Pin_1
  N9: Arduino1.D3, CONN1.d+
  N10: Arduino1.D2, CONN1.d-
  +5V: Arduino1.+5V, K2.COIL2, D2.cathode, CONN1.5V
  N11: K2.A, S2.leg0
  N12: K2.COIL1, D2.anode, Q2.C
  N13: R2.Pin_0, Q2.B

notes:
  Fingerprint
  Lock 1
  Lock 2
